# Fritzing sketch binaryclock (saved by Fritzing 0.9.3b)
breadboards: 2

parts:
  LED2 = smd LED [color="Blue (470nm)" package="1206 [SMD]"]
  LED7 = smd LED [color="Green (560nm)" package="1206 [SMD]"]
  LED6 = smd LED [color="White (6500K)" package="1206 [SMD]"]
  LED8 = smd LED [color="Green (560nm)" package="1206 [SMD]"]
  LED12 = smd LED [color="Red (635nm)" package="1206 [SMD]"]
  LED13 = smd LED [color="Red (635nm)" package="1206 [SMD]"]
  LED10 = smd LED [color="Green (560nm)" package="1206 [SMD]"]
  LED1 = smd LED [color="Blue (470nm)" package="1206 [SMD]"]
  LED5 = smd LED [color="Blue (470nm)" package="1206 [SMD]"]
  LED3 = smd LED [color="Blue (470nm)" package="1206 [SMD]"]
  LED11 = smd LED [color="Green (560nm)" package="1206 [SMD]"]
  LED4 = smd LED [color="Blue (470nm)" package="1206 [SMD]"]
  LED9 = smd LED [color="Green (560nm)" package="1206 [SMD]"]
  LED14 = smd LED [color="Red (635nm)" package="1206 [SMD]"]
  LED15 = smd LED [color="Red (635nm)" package="1206 [SMD]"]
  LED16 = smd LED [color="Red (635nm)" package="1206 [SMD]"]
  LED17 = smd LED [color="Green (560nm)" package="1206 [SMD]"]
  LED18 = smd LED [color="Red (635nm)" package="1206 [SMD]"]
  LED19 = smd LED [color="White (6500K)" package="1206 [SMD]"]
  LED20 = smd LED [color="White (6500K)" package="1206 [SMD]"]
  U1 = 74HC595 [package="DIP16 [THT]"]
  U2 = 74HC595 [package="DIP16 [THT]"]
  U3 = 74HC595 [package="DIP16 [THT]"]
  Bauteil1 = Arduino Nano (Rev3.0)
  ZS-042_RTC1 = ZS-042 RTC Module
  U4 = POT [package=pot_alpha_rv16af-20]
  S1 = Pushbutton [package="[SMD]"]
  S2 = Pushbutton [package="[SMD]"]
  S3 = Pushbutton [package="[SMD]"]

nets:
  N1: LED2.cathode, LED7.cathode, LED6.cathode, LED8.cathode, LED12.cathode, LED13.cathode, LED10.cathode, LED1.cathode, LED5.cathode, LED3.cathode, LED11.cathode, LED4.cathode, LED9.cathode, LED14.cathode, LED15.cathode, LED16.cathode, LED17.cathode, LED18.cathode
  N2: LED2.anode, U1.Q7
  N3: LED7.anode, U2.Q7
  N4: LED6.anode, Bauteil1.D9
  N5: LED8.anode, U2.Q6
  N6: LED12.anode, U3.Q7
  N7: LED13.anode, U3.Q6
  N8: LED10.anode, U2.Q4
  N9: LED1.anode, U1.Q4
  N10: LED5.anode, U1.Q3
  N11: LED3.anode, U1.Q6
  N12: LED11.anode, U2.Q3
  N13: LED4.anode, U1.Q5
  N14: LED9.anode, U2.Q5
  N15: LED14.anode, U3.Q5
  N16: LED15.anode, U3.Q4
  N17: LED16.anode, U3.Q3
  N18: LED17.anode, U2.Q2
  N19: LED18.anode, U3.Q2
  N20: LED19.cathode, LED20.cathode
  N21: LED19.anode, Bauteil1.D7
  N22: LED20.anode, Bauteil1.D8
  GND: U1.GND, U2.GND, U3.GND, S1.Pin_3, S1.Pin_4, S2.Pin_3, S2.Pin_4, S3.Pin_3, S3.Pin_4
  N23: U1.Q7', U2.DS
  VCC: U1.MR, U1.VCC, U2.MR, U2.VCC, U3.MR, U3.VCC, Bauteil1.5V, ZS-042_RTC1.VCC
  N24: U1.SH_CP, U2.SH_CP, U3.SH_CP, Bauteil1.D10
  N25: U1.ST_CP, U2.ST_CP, U3.ST_CP, Bauteil1.D11/MOSI
  N26: U1.OE, U2.OE, U3.OE, Bauteil1.D3
  N27: U1.DS, Bauteil1.D12/MISO
  N28: U2.Q7', U3.DS
  GND_2: Bauteil1.GND, ZS-042_RTC1.GND, U4.A
  N29: Bauteil1.D4, S1.Pin_1, S1.Pin_2
  N30: Bauteil1.D5, S2.Pin_1, S2.Pin_2
  N31: Bauteil1.D6, S3.Pin_1, S3.Pin_2
  N32: Bauteil1.A5, ZS-042_RTC1.SCL
  N33: Bauteil1.A4, ZS-042_RTC1.SDA
  N34: Bauteil1.A3, U4.S
