# Fritzing sketch pullupdown (saved by Fritzing 0.9.3b)
breadboards: 1

parts:
  Bauteil1 = Arduino Nano (Rev3.0)
  R1 = Resistor [tolerance=±5% resistance=220 package="0805 [SMD]"]
  R2 = Resistor [tolerance=±5% resistance=220 package="0805 [SMD]"]
  R4 = Resistor [tolerance=±5% resistance=10k package="0805 [SMD]"]
  LED1 = smd LED [color="Green (560nm)" package="1206 [SMD]"]
  LED2 = smd LED [color="Blue (470nm)" package="1206 [SMD]"]
  S1 = Pushbutton [package="[SMD]"]
  S2 = Pushbutton [package="[SMD]"]

nets:
  N1: Bauteil1.D6, S2.Pin_3, S2.Pin_4
  N2: Bauteil1.D7, S1.Pin_3, S1.Pin_4
  N3: Bauteil1.D11/MOSI, R2.Pin_1
  N4: Bauteil1.D12/MISO, R1.Pin_1
  N5: Bauteil1.GND, R4.Pin_1, LED1.cathode, LED2.cathode, S1.Pin_1, S1.Pin_2
  N6: Bauteil1.5V, R4.Pin_0, S2.Pin_1, S2.Pin_2
  N7: R1.Pin_0, LED1.anode
  N8: R2.Pin_0, LED2.anode
