# Fritzing sketch sevseg_multiplexing_schematic (saved by Fritzing 0.9.3b)
breadboards: 2

parts:
  Bauteil1 = Arduino Nano (Rev3.0)
  U1 = 74HC595 [package="DIP16 [THT]"]
  R1 = Resistor [tolerance=±5% resistance=220 package="2512 [SMD]"]
  R2 = Resistor [tolerance=±5% resistance=220 package="2512 [SMD]"]
  R3 = Resistor [tolerance=±5% resistance=220 package="2512 [SMD]"]
  R4 = Resistor [tolerance=±5% resistance=220 package="2512 [SMD]"]
  R5 = Resistor [tolerance=±5% resistance=220 package="2512 [SMD]"]
  R6 = Resistor [tolerance=±5% resistance=220 package="2512 [SMD]"]
  R7 = Resistor [tolerance=±5% resistance=220 package="2512 [SMD]"]
  R8 = Resistor [tolerance=±5% resistance=220 package="2512 [SMD]"]
  U2 = 7-SEGMENT-4DIGIT [package=7-segment-4digit]
  Q1 = NPN-Transistor [package="TO92 [THT]"]
  Q2 = NPN-Transistor [package="TO92 [THT]"]
  Q3 = NPN-Transistor [package="TO92 [THT]"]
  Q4 = NPN-Transistor [package="TO92 [THT]"]
  R9 = Resistor [tolerance=±5% resistance=10k package="2512 [SMD]"]
  R10 = Resistor [tolerance=±5% resistance=10k package="2512 [SMD]"]
  R11 = Resistor [tolerance=±5% resistance=10k package="2512 [SMD]"]
  R12 = Resistor [tolerance=±5% resistance=10k package="2512 [SMD]"]

nets:
  N1: Bauteil1.D5, U1.SH_CP
  N2: Bauteil1.D6, U1.ST_CP
  N3: Bauteil1.D7, U1.DS
  N4: Bauteil1.D10, R9.Pin_1
  N5: Bauteil1.D11/MOSI, R10.Pin_1
  N6: Bauteil1.D12/MISO, R11.Pin_1
  N7: Bauteil1.D13/SCK, R12.Pin_1
  N8: U1.Q1, R7.Pin_1
  N9: U1.Q2, R6.Pin_1
  N10: U1.Q3, R5.Pin_1
  N11: U1.Q4, R4.Pin_1
  N12: U1.Q5, R3.Pin_1
  N13: U1.Q6, R2.Pin_1
  N14: U1.Q7, R1.Pin_1
  N15: U1.GND, U1.OE
  N16: U1.Q7', U1.VCC
  N17: U1.Q0, R8.Pin_1
  N18: R1.Pin_0, U2.3
  N19: R2.Pin_0, U2.5
  N20: R3.Pin_0, U2.14
  N21: R4.Pin_0, U2.1
  N22: R5.Pin_0, U2.2
  N23: R6.Pin_0, U2.4
  N24: R7.Pin_0, U2.9
  N25: R8.Pin_0, U2.15
  N26: U2.6, Q4.B
  N27: U2.11, Q3.B
  N28: U2.13, Q2.B
  N29: U2.16, Q1.B
  N30: Q1.E, Q2.E, Q3.E, Q4.E
  N31: Q1.C, R12.Pin_0
  N32: Q2.C, R11.Pin_0
  N33: Q3.C, R10.Pin_0
  N34: Q4.C, R9.Pin_0
