# Fritzing sketch memorygame (saved by Fritzing 0.9.3b)
breadboards: 1

parts:
  LED1 = smd LED [color="Green (560nm)" package="0603 [SMD]"]
  LED2 = smd LED [color="Yellow (585nm)" package="0603 [SMD]"]
  LED3 = smd LED [color="Blue (470nm)" package="0603 [SMD]"]
  LED4 = smd LED [color="Red (633nm)" package="0603 [SMD]"]
  S1 = Pushbutton [package="[SMD]"]
  S2 = Pushbutton [package="[SMD]"]
  S3 = Pushbutton [package="[SMD]"]
  S4 = Pushbutton [package="[SMD]"]
  J1 = Piezo Speaker
  Bauteil2 = Arduino Nano (Rev3.0)
  R1 = Resistor [tolerance=±5% resistance=10k package="1206 [SMD]"]
  R2 = Resistor [tolerance=±5% resistance=10k package="1206 [SMD]"]
  R3 = Resistor [tolerance=±5% resistance=10k package="1206 [SMD]"]
  R4 = Resistor [tolerance=±5% resistance=10k package="1206 [SMD]"]

nets:
  N1: LED1.cathode, LED2.cathode, LED3.cathode, LED4.cathode, S3.Pin_1, S3.Pin_2, S3.Pin_3, S3.Pin_4, S4.Pin_1, S4.Pin_2, J1.pin1, Bauteil2.GND, R2.Pin_1
  N2: LED1.anode, Bauteil2.D9
  N3: LED2.anode, Bauteil2.D10
  N4: LED3.anode, Bauteil2.D11/MOSI
  N5: LED4.anode, Bauteil2.D12/MISO
  N6: S1.Pin_1, S1.Pin_2, S2.Pin_1, S2.Pin_2
  N7: S1.Pin_3, S1.Pin_4, S2.Pin_3, S2.Pin_4, S4.Pin_3, S4.Pin_4, Bauteil2.5V, R1.Pin_1, R3.Pin_1, R4.Pin_1
  N8: J1.pin2, Bauteil2.D6
  N9: Bauteil2.D2, R3.Pin_0
  N10: Bauteil2.D3, R2.Pin_0
  N11: Bauteil2.D4, R4.Pin_0
  N12: Bauteil2.D5, R1.Pin_0
